# Fritzing sketch toilite (saved by Fritzing 0.9.3b)
breadboards: 1

parts:
  U1 = attiny85 [package=dip]
  LED1 = RGB LED (com. cathode, rbg) [package="5 mm [THT]"]
  S1 = Pushbutton [package="[THT]"]
  R2 = Resistor [tolerance=±5% resistance=150 package="0603 [SMD]"]
  R3 = Resistor [tolerance=±5% resistance=100 package="0603 [SMD]"]
  R4 = Resistor [tolerance=±5% resistance=100 package="0603 [SMD]"]
  R5 = TRIMPOT [package=3386u]
  R6 = Resistor [tolerance=±5% resistance=100 package=THT]
  PIR1 = PIR sensor
  U2 = Voltage Regulator - 3.3V [package="TO220 [THT]"]
  C1 = Electrolytic Capacitor [capacitance=1μF package="0405 [SMD, electrolytic]"]
  C2 = Electrolytic Capacitor [capacitance=1μF package="0405 [SMD, electrolytic]"]
  VCC2 = Battery block 9V
  Q2 = NPN-Transistor [package="TO92 [THT]"]
  R1 = Photocell (LDR) [package=THT]
  Q3 = PNP-Transistor [package="TO92 [THT]"]
  R7 = Resistor [tolerance=±5% resistance=100k package="2512 [SMD]"]
  Q1 = NPN-Transistor [package="TO92 [THT]"]

nets:
  N1: U1.Pin_3, R2.Pin_1
  GND: U1.Pin_4, LED1.common_cathode, R5.CCW, R6.Pin_0, PIR1.GND, U2.GND, C1.-, C2.+, VCC2.-, R1.pin_0, Q1.E
  N2: U1.Pin_5, R4.Pin_1
  N3: U1.Pin_6, R3.Pin_1
  N4: U1.Pin_7, S1.Pin_1, S1.Pin_2, R6.Pin_1
  N5: U1.Pin_8, Q3.C
  N6: LED1.red_anode, R2.Pin_0
  N7: LED1.blue_anode, R4.Pin_0
  N8: LED1.green_anode, R3.Pin_0
  N9: S1.Pin_3, S1.Pin_4, R5.CW, PIR1.VDD, U2.output_voltage, C1.+, Q3.E, R7.Pin_0
  N10: R5.WIPER, R1.pin_1, Q1.B
  N11: PIR1.SIG, Q2.B
  N12: U2.input_voltage, C2.-, VCC2.+
  N13: Q2.E, Q1.C
  N14: Q2.C, Q3.B, R7.Pin_1
